# Fritzing sketch module3 (saved by Fritzing 0.9.3b)
breadboards: 1

parts:
  Gizwits_WiFi_Witty_ESP-12F1 = Gizwits WiFi Witty ESP-12F
  IRLB8723 = npn-Powertransistor [package="TO220 [THT]"]
  IRLB8722 = npn-Powertransistor [package="TO220 [THT]"]
  IRLB8724 = npn-Powertransistor [package="TO220 [THT]"]
  DC-DC_3_3<=12V = RioRand LM2596
  rf315_transmitter = mystery part, 3 pins [chip_label=?]
  R4 = Resistor [tolerance=±5% resistance=10k package="1206 [SMD]"]
  R2 = Resistor [tolerance=±5% resistance=10k package="1206 [SMD]"]
  R5 = Resistor [tolerance=±5% resistance=10k package="1206 [SMD]"]
  J1 = Camdenboss CTB0158-7 [part_number=CTB0158-7 package=THT]
  Part2 = BH1750

nets:
  N1: Gizwits_WiFi_Witty_ESP-12F1.GPIO16, rf315_transmitter.pin1
  N2: Gizwits_WiFi_Witty_ESP-12F1.GPIO14, Part2.SDA
  N3: Gizwits_WiFi_Witty_ESP-12F1.GPIO12, Part2.SCL
  N4: Gizwits_WiFi_Witty_ESP-12F1.GPIO13, R4.Pin_0
  VCC: Gizwits_WiFi_Witty_ESP-12F1.VCC, DC-DC_3_3<=12V.Pin_2, Part2.VCC
  GND: Gizwits_WiFi_Witty_ESP-12F1.GND, DC-DC_3_3<=12V.Pin_3, Part2.GND
  N5: Gizwits_WiFi_Witty_ESP-12F1.GPIO4, R5.Pin_0
  N6: Gizwits_WiFi_Witty_ESP-12F1.GPIO5, R2.Pin_0
  N7: IRLB8723.base, R5.Pin_1
  N8: IRLB8723.collector, J1.pin3
  N9: IRLB8723.emitter, IRLB8722.emitter, IRLB8724.emitter, rf315_transmitter.pin3, J1.pin7
  N10: IRLB8722.base, R2.Pin_1
  N11: IRLB8722.collector, J1.pin2
  N12: IRLB8724.base, R4.Pin_1
  N13: IRLB8724.collector, J1.pin1
  N14: rf315_transmitter.pin2, J1.pin6

notes:
  R G B + - 12V

custom parts:
  BH1750: Light Sensor
